# Fritzing sketch pi_pico_tft_display_pcb (saved by Fritzing 0.9.10b)
circuit board: 5.24821cm x 7.62686cm
perfboards: 1

parts:
  R1 = Resistor [tolerance=±5% power=0.25 resistance=220 package=THT]
  J1 = female pin header, 16 pins [form="♀ (female)"]
  PR1 = female pin header, 20 pins [form="♀ (female)"]
  PL = female pin header, 20 pins [form="♀ (female)"]
  R2 = Resistor [tolerance=±5% power=0.25 resistance=220 package=THT]

nets:
  N1: R1.Pin_0, PR1.pin16
  N2: R1.Pin_1, J1.pin2, J1.pin15, PR1.pin5, R2.Pin_1
  N3: J1.pin1, PR1.pin3
  N4: J1.pin6, PR1.pin19
  N5: J1.pin7, PR1.pin20
  N6: J1.pin8, PL.pin15
  N7: J1.pin9, PL.pin14
  N8: J1.pin10, PR1.pin17
  N9: PR1.pin15, R2.Pin_0

notes:
  ashishware.com
  GND
  VCC
  NC
  SDA
  AO
  RESET
  SCL
  MISO
  SD_CS
  MOSI
  LED+
  LED-
  CS
  SCK
  VOUT 3.3v
  GP20
  GP18
  GP16
  GP17
  GP21
  GP11
  GP10
  RST
  A0
